# Fritzing sketch Bread Board (saved by Fritzing 0.8.7b)
breadboards: 1

parts:
  Part1 = Arduino Uno (Rev3)
  IC1 = H-Bridge [package=THT]
  C1 = Electrolytic Capacitor [capacitance=1µF package="100 mil [THT, electrolytic]"]
  U1 = mystery part, 4 pins [chip_label=Bluetooth]
  M1 = DC Motor
  M2 = DC Motor

nets:
  N1: Part1.D8, IC1.3A
  N2: Part1.D9_PWM, IC1.4A
  N3: Part1.D10_PWM/SS, IC1.3_4EN
  N4: Part1.D0/RX, U1.pin4
  N5: Part1.D1/TX, U1.pin3
  N6: Part1.D3_PWM, IC1.1_2EN
  N7: Part1.D4, IC1.1A
  N8: Part1.D5_PWM, IC1.2A
  N9: Part1.5V, U1.pin1
  GND: Part1.GND, IC1.GND1, IC1.GND2, IC1.GND3, IC1.GND4, C1.-, U1.pin2
  N10: IC1.1Y, M2.pin_1
  N11: IC1.2Y, M2.pin_2
  N12: IC1.VCC2, IC1.VCC1, C1.+
  N13: IC1.3Y, M1.pin_1
  N14: IC1.4Y, M1.pin_2

notes:
  All done, now for the code!
